// Logisim project ALU.circ as structural Verilog: 1 circuit, main circuit ALU
module ALU (
  input  [31:0] A,
  input  [31:0] B,
  input  [4:0] Shift,
  input  [3:0] Codop,
  input  CarryIn,
  output [31:0] S,
  output [3:0] Flags,
  output [31:0] out_8
);

  wire adder_3_cout, bitselector_1_out, bitselector_2_out, C_ADC, C_CMN, C_CMP, C_SBC, comparator_1_gt,
       comparator_1_lt, comparator_2_gt, comparator_2_lt, comparator_3_eq, comparator_4_eq, comparator_5_gt,
       comparator_5_lt, comparator_6_gt, comparator_6_lt, comparator_7_gt, comparator_7_lt, comparator_8_gt,
       comparator_8_lt, not_3_out, not_5_out, or_2_out, or_3_out, or_4_out, or_5_out, or_6_out, or_7_out,
       subtractor_4_out, V_ADC, V_CMN, V_CMP, V_RSB, V_SBC;
  wire [4:0] adder_4_out, subtractor_5_out, subtractor_6_out;
  wire [31:0] not_1_out, not_4_out, OP_ADC, OP_AND, OP_ASR, OP_BIC, OP_CMN, OP_CMP, OP_EOR, OP_LSL, OP_LSR,
       OP_MUL, OP_MVN, OP_ORR, OP_ROR, OP_RSB, OP_SBC, OP_TST;

  assign OP_AND = A & B;  // AND_Gate and_1, 32 bits wide
  assign OP_EOR = A ^ B;  // XOR_Gate xor_1, 32 bits wide
  Shifter #(.width(32)) shifter_1 (.in(B), .\dist (Shift), .out(OP_LSL));
  Shifter #(.shift("lr"), .width(32)) shifter_2 (.in(B), .\dist (Shift), .out(OP_LSR));
  Shifter #(.shift("ar"), .width(32)) shifter_3 (.in(B), .\dist (Shift), .out(OP_ASR));
  Adder #(.width(32)) adder_1 (.a(A), .b(B), .out(OP_ADC), .cin(CarryIn), .cout(C_ADC));
  Subtractor #(.width(32)) subtractor_1 (.a(B), .b(A), .out(OP_SBC), .bin(subtractor_4_out), .bout(C_SBC));
  Shifter #(.shift("rr"), .width(32)) shifter_4 (.in(B), .\dist (Shift), .out(OP_ROR));
  assign OP_TST = A & B;  // AND_Gate and_2, 32 bits wide
  Subtractor #(.width(32)) subtractor_2 (.a({32{1'b0}}), .b(A), .out(OP_RSB));  // open: bin, bout
  Subtractor #(.width(32)) subtractor_3 (.a(B), .b(A), .out(OP_CMP), .bout(C_CMP));  // open: bin
  Adder #(.width(32)) adder_2 (.a(A), .b(B), .out(OP_CMN), .cout(C_CMN));  // open: cin
  assign OP_ORR = A | B;  // OR_Gate or_1, 32 bits wide
  Multiplier #(.width(32)) multiplier_1 (.a(A), .b(B), .out(OP_MUL));  // open: cin, cout
  assign not_1_out = ~A;  // NOT_Gate not_1, 32 bits wide
  assign OP_BIC = not_1_out & B;  // AND_Gate and_3, 32 bits wide
  assign OP_MVN = ~A;  // NOT_Gate not_2, 32 bits wide
  Subtractor #(.width(1)) subtractor_4 (.a(CarryIn), .b(1'b1), .out(subtractor_4_out));  // open: bin, bout
  not not_3 (not_3_out, C_SBC);
  assign not_4_out = ~A;  // NOT_Gate not_4, 32 bits wide
  not not_5 (not_5_out, C_CMP);
  Adder #(.width(32)) adder_3 (.a(not_4_out), .b(32'h1), .cout(adder_3_cout));  // open: out, cin
  Subtractor #(.width(5)) subtractor_5 (.a(Shift), .b(5'b00001), .out(subtractor_5_out));  // open: bin, bout
  Comparator #(.width(1)) comparator_1 (
    .a(OP_ADC[31]), .b(B[31]), .gt(comparator_1_gt), .lt(comparator_1_lt));  // open: eq
  Comparator #(.width(1)) comparator_2 (
    .a(OP_CMN[31]), .b(B[31]), .gt(comparator_2_gt), .lt(comparator_2_lt));  // open: eq
  BitSelector #(.width(32)) bitselector_1 (.in(B), .out(bitselector_1_out), .sel(subtractor_5_out));
  Comparator #(.width(1)) comparator_3 (.a(A[31]), .b(B[31]), .eq(comparator_3_eq));  // open: gt, lt
  or or_2 (or_2_out, comparator_1_gt, comparator_1_lt);
  Comparator #(.width(1)) comparator_4 (.a(A[31]), .b(B[31]), .eq(comparator_4_eq));  // open: gt, lt
  or or_3 (or_3_out, comparator_2_gt, comparator_2_lt);
  Comparator #(.width(1)) comparator_5 (.a(A[31]), .b(B[31]), .gt(comparator_5_gt), .lt(comparator_5_lt));  // open: eq
  Comparator #(.width(1)) comparator_6 (
    .a(OP_SBC[31]), .b(B[31]), .gt(comparator_6_gt), .lt(comparator_6_lt));  // open: eq
  Comparator #(.width(1)) comparator_7 (.a(A[31]), .b(B[31]), .gt(comparator_7_gt), .lt(comparator_7_lt));  // open: eq
  Comparator #(.width(1)) comparator_8 (
    .a(OP_CMP[31]), .b(B[31]), .gt(comparator_8_gt), .lt(comparator_8_lt));  // open: eq
  Comparator #(.width(32)) comparator_9 (.a(A), .b(32'h7fffffff), .eq(V_RSB));  // open: gt, lt
  BitSelector #(.width(32)) bitselector_2 (.in(B), .out(bitselector_2_out), .sel(adder_4_out));
  or or_4 (or_4_out, comparator_5_gt, comparator_5_lt);
  or or_5 (or_5_out, comparator_6_gt, comparator_6_lt);
  or or_6 (or_6_out, comparator_7_gt, comparator_7_lt);
  or or_7 (or_7_out, comparator_8_gt, comparator_8_lt);
  Multiplexer #(.select(4), .width(32)) multiplexer_1 (
    .in0(OP_AND), .in1(OP_EOR), .in2(OP_LSL), .in3(OP_LSR), .in4(OP_ASR), .in5(OP_ADC), .in6(OP_SBC),
    .in7(OP_ROR), .in8(B), .in9(OP_RSB), .in10(B), .in11(B), .in12(OP_ORR), .in13(OP_MUL), .in14(OP_BIC),
    .in15(OP_MVN), .out(S), .sel(Codop));
  and and_4 (V_ADC, comparator_3_eq, or_2_out);
  and and_5 (V_CMN, comparator_4_eq, or_3_out);
  Subtractor #(.width(5)) subtractor_6 (.a({5{1'b1}}), .b(Shift), .out(subtractor_6_out));  // open: bin, bout
  Multiplexer #(.select(4)) multiplexer_2 (
    .in0(1'b0), .in1(1'b0), .in2(bitselector_2_out), .in3(bitselector_1_out), .in4(bitselector_1_out),
    .in5(C_ADC), .in6(not_3_out), .in7(Flags[3]), .in8(1'b0), .in9(adder_3_cout), .in10(not_5_out),
    .in11(C_CMN), .in12(1'b0), .in13(1'b0), .in14(1'b0), .in15(1'b0), .out(Flags[1]), .sel(Codop));
  and and_6 (V_SBC, or_4_out, or_5_out);
  and and_7 (V_CMP, or_6_out, or_7_out);
  Multiplexer #(.select(4)) multiplexer_3 (
    .in0(1'b0), .in1(1'b0), .in2(1'b0), .in3(1'b0), .in4(1'b0), .in5(V_ADC), .in6(V_SBC), .in7(1'b0),
    .in8(1'b0), .in9(V_RSB), .in10(V_CMP), .in11(V_CMN), .in12(1'b0), .in13(1'b0), .in14(1'b0), .in15(1'b0),
    .out(Flags[0]), .sel(Codop));
  Adder #(.width(5)) adder_4 (.a(5'b00001), .b(subtractor_6_out), .out(adder_4_out));  // open: cin, cout
  Comparator #(.width(32)) comparator_10 (.a(out_8), .b({32{1'b0}}), .eq(Flags[2]), .lt(Flags[3]));  // open: gt
  Multiplexer #(.select(4), .width(32)) multiplexer_4 (
    .in0(S), .in1(S), .in2(S), .in3(S), .in4(S), .in5(S), .in6(S), .in7(S), .in8(OP_TST), .in9(S),
    .in10(OP_CMP), .in11(OP_CMN), .in12(S), .in13(S), .in14(S), .in15(S), .out(out_8), .sel(Codop));

  // Other names for the same wires on the sheet: V = Flags[0]; C = Flags[1]; Z = Flags[2]; N = Flags[3];
  //   FlagsZN[31:0] = out_8

  // Notes on the sheet:
  //   Note: for ROR, C = N
  //   Note 2: assume that shift > 0 for LSL and LSR
  //   Calcule le résultat pour chaque opération
  //   Renvoie C en fonction de Codop
  //   Calcule de V
  //   Renvoie V en fonction de codop
  //   Renvoie le résultat en fonction de Codop
endmodule
