// Logisim project Ctl_Conditional.circ as structural Verilog: 1 circuit, main circuit Conditional
module Conditional (
  input  Enable,
  input  [15:0] Instruction,
  input  Z,
  input  C,
  input  N,
  input  V,
  output [10:0] Offset,
  output Verified
);

  wire CC_LO, comparator_3_eq, comparator_4_gt, comparator_4_lt, comparator_5_eq, comparator_6_gt,
       comparator_6_lt, Cond, CS_HS, EQ, false, GE, GT, HI, LE, LS, LT, MI, NE, not_1_out, not_2_out,
       not_3_out, not_4_out, not_5_out, not_6_out, not_7_out, or_1_out, or_2_out, or_4_out, PL, Uncond, VC,
       VerifiedCond, VerifiedCond_AL, VerifiedCond_CC_LO, VerifiedCond_CS_HS, VerifiedCond_EQ,
       VerifiedCond_GE, VerifiedCond_GT, VerifiedCond_HI, VerifiedCond_LE, VerifiedCond_LS, VerifiedCond_LT,
       VerifiedCond_MI, VerifiedCond_NE, VerifiedCond_PL, VerifiedCond_VC, VerifiedCond_VS, VS;
  wire [3:0] bit_extender_1_out, CODE;
  wire [7:0] and_18_out, bit_extender_3_out;
  wire [10:0] bit_extender_2_out, bit_extender_4_out, Offset_COND, Offset_UNCOND, or_3_out;

  not not_1 (not_1_out, Z);
  not not_2 (not_2_out, N);
  not not_3 (not_3_out, V);
  not not_4 (not_4_out, Z);
  not not_5 (not_5_out, C);
  Comparator #(.width(4)) comparator_1 (.a(Instruction[15:12]), .b(4'b1101), .eq(Cond));  // open: gt, lt
  Comparator #(.width(5)) comparator_2 (.a(Instruction[15:11]), .b(5'b11100), .eq(Uncond));  // open: gt, lt
  assign bit_extender_1_out = {{3{Cond}}, Cond};  // Bit_Extender bit_extender_1
  not not_6 (not_6_out, C);
  Comparator #(.width(1)) comparator_3 (.a(V), .b(N), .eq(comparator_3_eq));  // open: gt, lt
  assign CODE = bit_extender_1_out & Instruction[11:8];  // AND_Gate and_1, 4 bits wide
  and and_2 (VerifiedCond_EQ, EQ, Z);
  and and_3 (VerifiedCond_NE, NE, not_1_out);
  and and_4 (VerifiedCond_CS_HS, CS_HS, C);
  and and_5 (VerifiedCond_CC_LO, CC_LO, not_6_out);
  and and_6 (VerifiedCond_MI, MI, N);
  and and_7 (VerifiedCond_PL, PL, not_2_out);
  and and_8 (VerifiedCond_VS, VS, V);
  and and_9 (VerifiedCond_VC, VC, not_3_out);
  and and_10 (VerifiedCond_HI, HI, C, not_4_out);
  and and_11 (VerifiedCond_LS, LS, Z, not_5_out);
  and and_12 (VerifiedCond_GE, GE, comparator_3_eq);
  or or_1 (or_1_out, comparator_4_gt, comparator_4_lt);
  Comparator #(.width(1)) comparator_4 (.a(V), .b(N), .gt(comparator_4_gt), .lt(comparator_4_lt));  // open: eq
  not not_7 (not_7_out, Z);
  Comparator #(.width(1)) comparator_5 (.a(V), .b(N), .eq(comparator_5_eq));  // open: gt, lt
  or or_2 (or_2_out, comparator_6_gt, comparator_6_lt);
  Comparator #(.width(1)) comparator_6 (.a(V), .b(N), .gt(comparator_6_gt), .lt(comparator_6_lt));  // open: eq
  assign bit_extender_2_out = {{10{Enable}}, Enable};  // Bit_Extender bit_extender_2
  and and_13 (VerifiedCond_LT, LT, or_1_out);
  and and_14 (VerifiedCond_GT, GT, not_7_out, comparator_5_eq);
  and and_15 (VerifiedCond_LE, LE, Z, or_2_out);
  assign or_3_out = Offset_COND | Offset_UNCOND;  // OR_Gate or_3, 11 bits wide
  Decoder #(.select(4)) decoder_1 (
    .out0(EQ), .out1(NE), .out2(CS_HS), .out3(CC_LO), .out4(MI), .out5(PL), .out6(VS), .out7(VC), .out8(HI),
    .out9(LS), .out10(GE), .out11(LT), .out12(GT), .out13(LE), .out14(VerifiedCond_AL), .out15(false),
    .sel(CODE), .en(Cond));
  assign Offset = or_3_out & bit_extender_2_out;  // AND_Gate and_16, 11 bits wide
  and and_17 (Verified, Enable, or_4_out);
  or or_4 (or_4_out, Uncond, VerifiedCond);
  assign bit_extender_3_out = {{7{Cond}}, Cond};  // Bit_Extender bit_extender_3
  assign bit_extender_4_out = {{10{Uncond}}, Uncond};  // Bit_Extender bit_extender_4
  or or_5 (VerifiedCond, VerifiedCond_EQ, VerifiedCond_NE, VerifiedCond_CS_HS, VerifiedCond_CC_LO, VerifiedCond_MI, VerifiedCond_PL, VerifiedCond_VS, VerifiedCond_AL, VerifiedCond_VC, VerifiedCond_HI, VerifiedCond_LS, VerifiedCond_GE, VerifiedCond_LT, VerifiedCond_GT, VerifiedCond_LE);
  assign and_18_out = bit_extender_3_out & Instruction[7:0];  // AND_Gate and_18, 8 bits wide
  assign Offset_UNCOND = bit_extender_4_out & Instruction[10:0];  // AND_Gate and_19, 11 bits wide
  assign Offset_COND = {{3{and_18_out[7]}}, and_18_out};  // Bit_Extender bit_extender_5
endmodule
