// Logisim project Ctl_Data_Processing.circ as structural Verilog: 1 circuit, main circuit Data_Processing
module Data_Processing (
  input  Enable,
  input  [15:0] Instruction,
  output [2:0] Rd,
  output [2:0] Rn,
  output [2:0] Rm,
  output [3:0] ALU_Opcode,
  output [3:0] Flags_Update_Mask
);

  wire C, decoder_1_out5, decoder_1_out6, decoder_1_out9, decoder_1_out10, decoder_1_out11, decoder_1_out13;
  wire [0:0] Flags;

  Decoder #(.select(4)) decoder_1 (
    .out5(decoder_1_out5), .out6(decoder_1_out6), .out9(decoder_1_out9), .out10(decoder_1_out10),
    .out11(decoder_1_out11), .out13(decoder_1_out13), .sel(Instruction[9:6]));  // open: out0, out1, out2, out3, out4, out7, out8, out12, out14, out15, en
  or or_1 (Flags[0], decoder_1_out11, decoder_1_out10, decoder_1_out9, decoder_1_out6, decoder_1_out5);
  not not_1 (C, decoder_1_out13);
  Multiplexer #(.width(3)) multiplexer_1 (.in0(3'b000), .in1(Instruction[2:0]), .out(Rd), .sel(Enable));
  Multiplexer #(.width(3)) multiplexer_2 (.in0(3'b000), .in1(Instruction[2:0]), .out(Rn), .sel(Enable));
  Multiplexer #(.width(3)) multiplexer_3 (.in0(3'b000), .in1(Instruction[5:3]), .out(Rm), .sel(Enable));
  Multiplexer #(.width(4)) multiplexer_4 (.in0(4'b0000), .in1(Instruction[9:6]), .out(ALU_Opcode), .sel(Enable));
  Multiplexer #(.width(4)) multiplexer_5 (
    .in0(4'b0000), .in1({2'b11, C, Flags[0]}), .out(Flags_Update_Mask), .sel(Enable));

  // Other names for the same wires on the sheet: V = Flags[0]; Flags[1] = C; Rnd[2:0] = Instruction[2:0];
  //   Rm_t[2:0] = Instruction[5:3]; OpCode[3:0] = Instruction[9:6]

  // Notes on the sheet:
  //   Note 2: RSB instruction has Rn as 1st operand.
  //   MUL instruction has Rn as 1st operand and Rdm as 2nd operand
  //   For simplification purposes, Rm is used for 1st operand both here and in the ALU.
  //   Note: instructions that does not save the result will still have the second operand as the destination register, the ALU will copy the second register to the destination register
  //   Pull output low on Enable = 0
endmodule
