// Logisim project Ctl_Load_Store.circ as structural Verilog: 1 circuit, main circuit Load_Store
module Load_Store (
  input  [15:0] Instruction,
  input  Enable,
  input  Clk,
  input  Reset,
  input  [31:0] Stack_Pointer,
  output Store,
  output Load,
  output PC_Hold,
  output [2:0] Rmd,
  output [31:0] RAM_Addr
);

  wire d_ff_1_q, xor_1_out;
  wire [2:0] bit_extender_3_out;
  wire [31:0] adder_1_out, bit_extender_1_out, bit_extender_2_out;

  assign bit_extender_1_out = {{24{1'b0}}, Instruction[7:0]};  // Bit_Extender bit_extender_1
  assign bit_extender_2_out = {{31{Enable}}, Enable};  // Bit_Extender bit_extender_2
  Adder #(.width(32)) adder_1 (.a(Stack_Pointer), .b(bit_extender_1_out), .out(adder_1_out));  // open: cin, cout
  assign RAM_Addr = bit_extender_2_out & adder_1_out;  // AND_Gate and_1, 32 bits wide
  D_Flip_Flop d_ff_1 (.D(xor_1_out), .clk(Clk), .Q(d_ff_1_q), .reset(Reset));  // open: Qn, preset
  xor xor_1 (xor_1_out, d_ff_1_q, Load);
  and and_2 (PC_Hold, Enable, d_ff_1_q);
  assign bit_extender_3_out = {{2{Enable}}, Enable};  // Bit_Extender bit_extender_3
  assign Rmd = bit_extender_3_out & Instruction[10:8];  // AND_Gate and_3, 3 bits wide
  Decoder decoder_1 (.out0(Store), .out1(Load), .sel(Instruction[11]), .en(Enable));

  // Other names for the same wires on the sheet: HOLD = PC_Hold; LDR = Load; SP[31:0] = Stack_Pointer; STR = Store

  // Notes on the sheet:
  //   Instruction: pull=down
  //   Calcul la RAM_Addr
  //   Load ou store
  //   Delay load and hold PC for 1 cycle for the RAM to send out requested data 
endmodule
