// Logisim project Ctl_SP_Address.circ as structural Verilog: 1 circuit, main circuit SP_Address
module SP_Address (
  input  [31:0] Stack_Pointer,
  input  [15:0] Instruction,
  input  Enable,
  output [31:0] New_Stack_Pointer,
  output Write_Enable,
  output [31:0] out_6
);

  wire ADD, SUB;
  wire [6:0] and_1_out, and_2_out, bit_extender_1_out, bit_extender_2_out;
  wire [31:0] bit_extender_3_out, bit_extender_4_out, SP_OUT_ADD;

  Decoder decoder_1 (.out0(ADD), .out1(SUB), .sel(Instruction[7]));  // open: en
  assign bit_extender_1_out = {{6{ADD}}, ADD};  // Bit_Extender bit_extender_1
  assign bit_extender_2_out = {{6{SUB}}, SUB};  // Bit_Extender bit_extender_2
  assign and_1_out = bit_extender_1_out & Instruction[6:0];  // AND_Gate and_1, 7 bits wide
  assign and_2_out = bit_extender_2_out & Instruction[6:0];  // AND_Gate and_2, 7 bits wide
  Adder #(.width(32)) adder_1 (.a(Stack_Pointer), .b(bit_extender_3_out), .out(SP_OUT_ADD));  // open: cin, cout
  assign bit_extender_3_out = {{25{1'b0}}, and_1_out};  // Bit_Extender bit_extender_3
  Subtractor #(.width(32)) subtractor_1 (.a(Stack_Pointer), .b(bit_extender_4_out), .out(out_6));  // open: bin, bout
  assign bit_extender_4_out = {{25{1'b0}}, and_2_out};  // Bit_Extender bit_extender_4
  Multiplexer #(.width(32)) multiplexer_1 (
    .in0(SP_OUT_ADD), .in1(out_6), .out(New_Stack_Pointer), .sel(Instruction[7]));

  assign Write_Enable = Enable;

  // Other names for the same wires on the sheet: SP[31:0] = Stack_Pointer; SP_OUT[31:0] = New_Stack_Pointer;
  //   SP_OUT_SUB[31:0] = out_6

  // Notes on the sheet:
  //   Pull output low on Enable = 0
endmodule
