// Logisim project Ctl_Shift_Add_Sub_Mov.circ as structural Verilog: 1 circuit, main circuit Shift_Add_Sub_Mov
module Shift_Add_Sub_Mov (
  input  Enable,
  input  [15:0] Instruction,
  output [3:0] Flags_Update_Mask,
  output Carry,
  output Imm32_Enable,
  output [2:0] Rm,
  output [2:0] Rn,
  output [2:0] Rd,
  output [4:0] Imm5,
  output [31:0] Imm32,
  output [3:0] ALU_Opcode
);

  wire ADDImm3, ADDImm8, ADDReg, ASROP, CMPOP, LSLOP, LSROP, MOVOP, SUBADDOP, SUBImm3, SUBImm8, SUBReg;
  wire [2:0] bit_extender_1_out, bit_extender_3_out, bit_extender_4_out, bit_extender_6_out,
       bit_extender_8_out, bit_extender_9_out, bit_extender_12_out, bit_extender_13_out, bit_extender_17_out,
       bit_extender_18_out, bit_extender_22_out, bit_extender_23_out, bit_extender_27_out,
       bit_extender_28_out, bit_extender_32_out, bit_extender_33_out, bit_extender_39_out,
       bit_extender_43_out, bit_extender_46_out, bit_extender_50_out, RdADDImm3, RdADDImm8, RdADDReg, RdASR,
       RdCMP, RdLSL, RdLSR, RdMOV, RdSUBImm3, RdSUBImm8, RdSUBReg, RmADDReg, RmSUBReg, RnADDImm3, RnADDReg,
       RnASR, RnLSL, RnLSR, RnSUBImm3, RnSUBReg;
  wire [3:0] bit_extender_2_out, bit_extender_5_out, bit_extender_7_out, bit_extender_10_out,
       bit_extender_11_out, bit_extender_14_out, bit_extender_16_out, bit_extender_19_out,
       bit_extender_21_out, bit_extender_24_out, bit_extender_26_out, bit_extender_29_out,
       bit_extender_31_out, bit_extender_34_out, bit_extender_38_out, bit_extender_40_out,
       bit_extender_42_out, bit_extender_44_out, bit_extender_45_out, bit_extender_47_out,
       bit_extender_49_out, bit_extender_51_out, CodopADDImm3, CodopADDImm8, CodopADDReg, CodopASR, CodopCMP,
       CodopLSL, CodopLSR, CodopMOV, CodopSUBADD, CodopSUBImm3, CodopSUBImm8, CodopSUBReg,
       FlagsUpdateADDImm3, FlagsUpdateADDImm8, FlagsUpdateADDReg, FlagsUpdateASR, FlagsUpdateCMP,
       FlagsUpdateLSL, FlagsUpdateLSR, FlagsUpdateMOV, FlagsUpdateSUBImm3, FlagsUpdateSUBImm8,
       FlagsUpdateSUBReg;
  wire [4:0] bit_extender_20_out, bit_extender_25_out, bit_extender_30_out, Imm5ASR, Imm5LSL, Imm5LSR, OP;
  wire [10:0] Res;
  wire [31:0] and_17_out, bit_extender_15_out, bit_extender_35_out, bit_extender_36_out, bit_extender_37_out,
       bit_extender_41_out, bit_extender_48_out, bit_extender_52_out, bit_extender_53_out,
       bit_extender_54_out, bit_extender_55_out, bit_extender_56_out, bit_extender_57_out, Imm32ADDImm3,
       Imm32ADDImm8, Imm32CMP, Imm32MOV, Imm32SUBImm3, Imm32SUBImm8;

  Multiplexer #(.width(16)) multiplexer_1 (.in0({16{1'b0}}), .in1(Instruction), .out({OP, Res}), .sel(Enable));
  Decoder #(.select(5)) decoder_1 (
    .out0(LSLOP), .out1(LSROP), .out2(ASROP), .out3(SUBADDOP), .out4(MOVOP), .out5(CMPOP), .out6(ADDImm8),
    .out7(SUBImm8), .sel(OP), .en(Enable));  // open: out8, out9, out10, out11, out12, out13, out14, out15, out16, out17, out18, out19, out20, out21, out22, out23, out24, out25, out26, out27, out28, out29, out30, out31
  assign ALU_Opcode = CodopLSL | CodopLSR | CodopASR | CodopSUBADD | CodopMOV | CodopCMP | CodopADDImm8 | CodopSUBImm8;  // OR_Gate or_1, 4 bits wide
  assign Rm = RmADDReg | RmSUBReg;  // OR_Gate or_2, 3 bits wide
  assign Rd = RdCMP | RdMOV | RdLSL | RdLSR | RdASR | RdADDReg | RdSUBReg | RdADDImm3 | RdSUBImm3 | RdADDImm8 | RdSUBImm8;  // OR_Gate or_3, 3 bits wide
  Comparator #(.width(4)) comparator_1 (.a(ALU_Opcode), .b(4'b0110), .eq(Carry));  // open: gt, lt
  or or_4 (Imm32_Enable, ADDImm8, ADDImm3, SUBImm3, MOVOP, CMPOP, SUBImm8);
  Multiplexer #(.select(2), .width(4)) multiplexer_2 (
    .in0(CodopADDReg), .in1(CodopSUBReg), .in2(CodopADDImm3), .in3(CodopSUBImm3), .out(CodopSUBADD),
    .sel(Res[10:9]));
  assign Imm5 = Imm5LSL | Imm5LSR | Imm5ASR;  // OR_Gate or_5, 5 bits wide
  assign Flags_Update_Mask = FlagsUpdateLSL | FlagsUpdateLSR | FlagsUpdateASR | FlagsUpdateADDReg | FlagsUpdateSUBReg | FlagsUpdateADDImm3 | FlagsUpdateSUBImm3 | FlagsUpdateMOV | FlagsUpdateCMP | FlagsUpdateADDImm8 | FlagsUpdateSUBImm8;  // OR_Gate or_6, 4 bits wide
  assign Rn = RnLSL | RnLSR | RnASR | RnADDReg | RnSUBReg | RnADDImm3 | RnSUBImm3;  // OR_Gate or_7, 3 bits wide
  assign Imm32 = Imm32ADDImm3 | Imm32SUBImm3 | Imm32MOV | Imm32CMP | Imm32ADDImm8 | Imm32SUBImm8;  // OR_Gate or_8, 32 bits wide
  assign bit_extender_1_out = {{2{ADDReg}}, ADDReg};  // Bit_Extender bit_extender_1
  assign bit_extender_2_out = {{3{ADDReg}}, ADDReg};  // Bit_Extender bit_extender_2
  assign bit_extender_3_out = {{2{ADDReg}}, ADDReg};  // Bit_Extender bit_extender_3
  assign bit_extender_4_out = {{2{ADDReg}}, ADDReg};  // Bit_Extender bit_extender_4
  assign bit_extender_5_out = {{3{ADDReg}}, ADDReg};  // Bit_Extender bit_extender_5
  assign bit_extender_6_out = {{2{SUBReg}}, SUBReg};  // Bit_Extender bit_extender_6
  assign bit_extender_7_out = {{3{SUBReg}}, SUBReg};  // Bit_Extender bit_extender_7
  assign bit_extender_8_out = {{2{SUBReg}}, SUBReg};  // Bit_Extender bit_extender_8
  assign bit_extender_9_out = {{2{SUBReg}}, SUBReg};  // Bit_Extender bit_extender_9
  assign bit_extender_10_out = {{3{SUBReg}}, SUBReg};  // Bit_Extender bit_extender_10
  assign bit_extender_11_out = {{3{ADDImm3}}, ADDImm3};  // Bit_Extender bit_extender_11
  assign bit_extender_12_out = {{2{ADDImm3}}, ADDImm3};  // Bit_Extender bit_extender_12
  assign bit_extender_13_out = {{2{ADDImm3}}, ADDImm3};  // Bit_Extender bit_extender_13
  assign bit_extender_14_out = {{3{ADDImm3}}, ADDImm3};  // Bit_Extender bit_extender_14
  assign bit_extender_15_out = {{31{SUBImm3}}, SUBImm3};  // Bit_Extender bit_extender_15
  assign bit_extender_16_out = {{3{SUBImm3}}, SUBImm3};  // Bit_Extender bit_extender_16
  assign bit_extender_17_out = {{2{SUBImm3}}, SUBImm3};  // Bit_Extender bit_extender_17
  assign bit_extender_18_out = {{2{SUBImm3}}, SUBImm3};  // Bit_Extender bit_extender_18
  assign bit_extender_19_out = {{3{SUBImm3}}, SUBImm3};  // Bit_Extender bit_extender_19
  assign bit_extender_20_out = {{4{LSLOP}}, LSLOP};  // Bit_Extender bit_extender_20
  assign bit_extender_21_out = {{3{LSLOP}}, LSLOP};  // Bit_Extender bit_extender_21
  assign bit_extender_22_out = {{2{LSLOP}}, LSLOP};  // Bit_Extender bit_extender_22
  assign bit_extender_23_out = {{2{LSLOP}}, LSLOP};  // Bit_Extender bit_extender_23
  assign bit_extender_24_out = {{3{LSLOP}}, LSLOP};  // Bit_Extender bit_extender_24
  assign bit_extender_25_out = {{4{LSROP}}, LSROP};  // Bit_Extender bit_extender_25
  assign bit_extender_26_out = {{3{LSROP}}, LSROP};  // Bit_Extender bit_extender_26
  assign bit_extender_27_out = {{2{LSROP}}, LSROP};  // Bit_Extender bit_extender_27
  assign bit_extender_28_out = {{2{LSROP}}, LSROP};  // Bit_Extender bit_extender_28
  assign bit_extender_29_out = {{3{LSROP}}, LSROP};  // Bit_Extender bit_extender_29
  assign bit_extender_30_out = {{4{ASROP}}, ASROP};  // Bit_Extender bit_extender_30
  assign bit_extender_31_out = {{3{ASROP}}, ASROP};  // Bit_Extender bit_extender_31
  assign bit_extender_32_out = {{2{ASROP}}, ASROP};  // Bit_Extender bit_extender_32
  assign bit_extender_33_out = {{2{ASROP}}, ASROP};  // Bit_Extender bit_extender_33
  assign bit_extender_34_out = {{3{ASROP}}, ASROP};  // Bit_Extender bit_extender_34
  Decoder #(.select(2)) decoder_2 (
    .out0(ADDReg), .out1(SUBReg), .out2(ADDImm3), .out3(SUBImm3), .sel(Res[10:9]), .en(SUBADDOP));
  assign bit_extender_35_out = {{31{ADDImm3}}, ADDImm3};  // Bit_Extender bit_extender_35
  assign bit_extender_36_out = {{29{1'b0}}, Res[8:6]};  // Bit_Extender bit_extender_36
  assign bit_extender_37_out = {{31{MOVOP}}, MOVOP};  // Bit_Extender bit_extender_37
  assign bit_extender_38_out = {{3{MOVOP}}, MOVOP};  // Bit_Extender bit_extender_38
  assign bit_extender_39_out = {{2{MOVOP}}, MOVOP};  // Bit_Extender bit_extender_39
  assign bit_extender_40_out = {{3{MOVOP}}, MOVOP};  // Bit_Extender bit_extender_40
  assign bit_extender_41_out = {{31{CMPOP}}, CMPOP};  // Bit_Extender bit_extender_41
  assign bit_extender_42_out = {{3{CMPOP}}, CMPOP};  // Bit_Extender bit_extender_42
  assign bit_extender_43_out = {{2{CMPOP}}, CMPOP};  // Bit_Extender bit_extender_43
  assign bit_extender_44_out = {{3{CMPOP}}, CMPOP};  // Bit_Extender bit_extender_44
  assign bit_extender_45_out = {{3{ADDImm8}}, ADDImm8};  // Bit_Extender bit_extender_45
  assign bit_extender_46_out = {{2{ADDImm8}}, ADDImm8};  // Bit_Extender bit_extender_46
  assign bit_extender_47_out = {{3{ADDImm8}}, ADDImm8};  // Bit_Extender bit_extender_47
  assign bit_extender_48_out = {{31{SUBImm8}}, SUBImm8};  // Bit_Extender bit_extender_48
  assign bit_extender_49_out = {{3{SUBImm8}}, SUBImm8};  // Bit_Extender bit_extender_49
  assign bit_extender_50_out = {{2{SUBImm8}}, SUBImm8};  // Bit_Extender bit_extender_50
  assign bit_extender_51_out = {{3{SUBImm8}}, SUBImm8};  // Bit_Extender bit_extender_51
  assign RmADDReg = Res[8:6] & bit_extender_1_out;  // AND_Gate and_1, 3 bits wide
  assign RnADDReg = Res[5:3] & bit_extender_3_out;  // AND_Gate and_2, 3 bits wide
  assign RdADDReg = Res[2:0] & bit_extender_4_out;  // AND_Gate and_3, 3 bits wide
  assign FlagsUpdateADDReg = 4'b1111 & bit_extender_5_out;  // AND_Gate and_4, 4 bits wide
  assign RmSUBReg = Res[8:6] & bit_extender_6_out;  // AND_Gate and_5, 3 bits wide
  assign RnSUBReg = Res[5:3] & bit_extender_8_out;  // AND_Gate and_6, 3 bits wide
  assign RdSUBReg = Res[2:0] & bit_extender_9_out;  // AND_Gate and_7, 3 bits wide
  assign FlagsUpdateSUBReg = 4'b1111 & bit_extender_10_out;  // AND_Gate and_8, 4 bits wide
  assign bit_extender_52_out = {{29{1'b0}}, Res[8:6]};  // Bit_Extender bit_extender_52
  assign Imm32ADDImm3 = bit_extender_52_out & bit_extender_35_out;  // AND_Gate and_9, 32 bits wide
  assign RnADDImm3 = Res[5:3] & bit_extender_12_out;  // AND_Gate and_10, 3 bits wide
  assign RdADDImm3 = Res[2:0] & bit_extender_13_out;  // AND_Gate and_11, 3 bits wide
  assign FlagsUpdateADDImm3 = 4'b1111 & bit_extender_14_out;  // AND_Gate and_12, 4 bits wide
  assign Imm32SUBImm3 = bit_extender_36_out & bit_extender_15_out;  // AND_Gate and_13, 32 bits wide
  assign RnSUBImm3 = Res[5:3] & bit_extender_17_out;  // AND_Gate and_14, 3 bits wide
  assign RdSUBImm3 = Res[2:0] & bit_extender_18_out;  // AND_Gate and_15, 3 bits wide
  assign FlagsUpdateSUBImm3 = 4'b1111 & bit_extender_19_out;  // AND_Gate and_16, 4 bits wide
  assign bit_extender_53_out = {{24{1'b0}}, Res[7:0]};  // Bit_Extender bit_extender_53
  assign and_17_out = bit_extender_53_out & bit_extender_37_out;  // AND_Gate and_17, 32 bits wide
  assign bit_extender_54_out = {{24{1'b0}}, Res[7:0]};  // Bit_Extender bit_extender_54
  assign Imm32CMP = bit_extender_54_out & bit_extender_41_out;  // AND_Gate and_18, 32 bits wide
  assign bit_extender_55_out = {{31{ADDImm8}}, ADDImm8};  // Bit_Extender bit_extender_55
  assign bit_extender_56_out = {{24{1'b0}}, Res[7:0]};  // Bit_Extender bit_extender_56
  assign Imm5LSL = Res[10:6] & bit_extender_20_out;  // AND_Gate and_19, 5 bits wide
  assign CodopLSL = 4'b0010 & bit_extender_21_out;  // AND_Gate and_20, 4 bits wide
  assign RnLSL = Res[5:3] & bit_extender_22_out;  // AND_Gate and_21, 3 bits wide
  assign RdLSL = Res[2:0] & bit_extender_23_out;  // AND_Gate and_22, 3 bits wide
  assign FlagsUpdateLSL = 4'b1110 & bit_extender_24_out;  // AND_Gate and_23, 4 bits wide
  assign Imm5LSR = Res[10:6] & bit_extender_25_out;  // AND_Gate and_24, 5 bits wide
  assign CodopLSR = 4'b0011 & bit_extender_26_out;  // AND_Gate and_25, 4 bits wide
  assign RnLSR = Res[5:3] & bit_extender_27_out;  // AND_Gate and_26, 3 bits wide
  assign RdLSR = Res[2:0] & bit_extender_28_out;  // AND_Gate and_27, 3 bits wide
  assign FlagsUpdateLSR = 4'b1110 & bit_extender_29_out;  // AND_Gate and_28, 4 bits wide
  assign Imm5ASR = Res[10:6] & bit_extender_30_out;  // AND_Gate and_29, 5 bits wide
  assign CodopASR = 4'b0100 & bit_extender_31_out;  // AND_Gate and_30, 4 bits wide
  assign RnASR = Res[5:3] & bit_extender_32_out;  // AND_Gate and_31, 3 bits wide
  assign RdASR = Res[2:0] & bit_extender_33_out;  // AND_Gate and_32, 3 bits wide
  assign FlagsUpdateASR = 4'b1110 & bit_extender_34_out;  // AND_Gate and_33, 4 bits wide
  assign CodopADDReg = 4'b0101 & bit_extender_2_out;  // AND_Gate and_34, 4 bits wide
  assign CodopSUBReg = 4'b0110 & bit_extender_7_out;  // AND_Gate and_35, 4 bits wide
  assign CodopADDImm3 = 4'b0101 & bit_extender_11_out;  // AND_Gate and_36, 4 bits wide
  assign CodopSUBImm3 = 4'b0110 & bit_extender_16_out;  // AND_Gate and_37, 4 bits wide
  Negator #(.width(32)) negator_1 (.in(and_17_out), .out(Imm32MOV));
  assign CodopMOV = 4'b1001 & bit_extender_38_out;  // AND_Gate and_38, 4 bits wide
  assign RdMOV = Res[10:8] & bit_extender_39_out;  // AND_Gate and_39, 3 bits wide
  assign FlagsUpdateMOV = 4'b1100 & bit_extender_40_out;  // AND_Gate and_40, 4 bits wide
  assign CodopCMP = 4'b1010 & bit_extender_42_out;  // AND_Gate and_41, 4 bits wide
  assign RdCMP = Res[10:8] & bit_extender_43_out;  // AND_Gate and_42, 3 bits wide
  assign FlagsUpdateCMP = 4'b1111 & bit_extender_44_out;  // AND_Gate and_43, 4 bits wide
  assign bit_extender_57_out = {{24{1'b0}}, Res[7:0]};  // Bit_Extender bit_extender_57
  assign Imm32ADDImm8 = bit_extender_57_out & bit_extender_55_out;  // AND_Gate and_44, 32 bits wide
  assign RdADDImm8 = Res[10:8] & bit_extender_46_out;  // AND_Gate and_45, 3 bits wide
  assign FlagsUpdateADDImm8 = 4'b1111 & bit_extender_47_out;  // AND_Gate and_46, 4 bits wide
  assign Imm32SUBImm8 = bit_extender_56_out & bit_extender_48_out;  // AND_Gate and_47, 32 bits wide
  assign RdSUBImm8 = Res[10:8] & bit_extender_50_out;  // AND_Gate and_48, 3 bits wide
  assign FlagsUpdateSUBImm8 = 4'b1111 & bit_extender_51_out;  // AND_Gate and_49, 4 bits wide
  assign CodopADDImm8 = 4'b0101 & bit_extender_45_out;  // AND_Gate and_50, 4 bits wide
  assign CodopSUBImm8 = 4'b0110 & bit_extender_49_out;  // AND_Gate and_51, 4 bits wide

  // Other names for the same wires on the sheet: Codop[3:0] = ALU_Opcode; Res[15:11] = OP;
  //   UpdateMask[3:0] = Flags_Update_Mask

  // Notes on the sheet:
  //   Active la bonne opération
  //   Note: ALU uses Rn register for shifts. Use Rn instead of Rm for shifts (immediate) here too
  //   Note 2: MOV uses RSB ALU opcode with Imm8 reversed so that it is copied to output register
  //   Note 3: Imm32_Enable forces the use of the immediate for Rm register
  //   Pull output low on Enable = 0
  //   Renvoie les sorties nécessaire pour les ADD/SUB Imm3 et registre
  //   Renvoie les sorties nécessaire pour les shifts
  //   Active le bon SUB ou ADD (Imm3 ou registre)
  //   Active MOV et CMP
  //   Active SUB et ADD Imm8
  //   only ADD and SUB use Rm
  //   Enable carry for SUB since it is reversed in ALU
  //   ALU will use Imm32 instead of Rm
endmodule
